# Fritzing sketch ESP32-JablotronUnit (saved by Fritzing 0.9.3b)

parts:
  RS485_module1 = RS485 Module (MAX3485)
  U1 = LuaNode32 / ESP32

nets:
  GND: RS485_module1.GND, U1.GND
  VCC: RS485_module1.VCC, U1.3V3
  N1: RS485_module1.RO, U1.RX2
  N2: RS485_module1.RE, RS485_module1.DE, U1.D4
  N3: RS485_module1.DI, U1.TX2

custom parts:
  RS485 Module (MAX3485): Commercially available RS485 to RS232 TTL Module
  LuaNode32 / ESP32: ESP32 based LuaNode32
