# Fritzing sketch NodeMCU-HeatingRealy (saved by Fritzing 0.9.3b)

parts:
  WeMos_D1_Mini1 = WeMos D1 Mini
  KY-3 = Keyes Relay [part_number="Hot Water Pump" package=THT]
  KY-4 = Keyes Relay [part_number=Heating package=THT]

nets:
  N1: WeMos_D1_Mini1.5V, KY-3.power, KY-4.power
  N2: WeMos_D1_Mini1.D1, KY-4.signal
  N3: WeMos_D1_Mini1.D2, KY-3.signal
  N4: WeMos_D1_Mini1.G, KY-3.ground, KY-4.ground
  N5: KY-3.C, KY-3.NO
  N6: KY-4.C, KY-4.NO

custom parts:
  Keyes Relay: The Keyes 5V relay module is suitable for SCM development, home appliance control. It uses a 5V~12V TIL control signal which can control DC / AC signal.
