# Fritzing sketch OutdoorUnit (saved by Fritzing 0.9.3b)

parts:
  Raspberry_Pi1 = Raspberry Pi B rev2
  DS1 = DS18B20 1-Wire Temperature Sensor [part_number=DS18B20]
  R1 = Resistor [tolerance=±5% resistance=4.7k package=THT]
  Q1 = NPN-Transistor [package="TO92 [THT]"]
  R2 = Resistor [tolerance=±5% resistance=4.7k package=THT]
  R3 = Resistor [tolerance=±5% resistance=4.7k package=THT]
  R4 = Resistor [tolerance=±5% resistance=47k package=THT]
  JP1 = Header 1 [part_number="Moisture In +" package=1x01_offset]
  JP2 = Header 1 [part_number="Moisture In -" package=1x01_offset]
  U1 = RELAY [part_number="5V Relay" package=relay-t9a]
  Q2 = NPN-Transistor [package="TO92 [THT]"]
  R5 = Resistor [tolerance=±5% resistance=4.7k package=THT]

nets:
  3V3: Raspberry_Pi1.3V3, DS1.VDD, R1.Pin_0, R2.Pin_0
  N1: Raspberry_Pi1.5V, R4.Pin_0, U1.COIL1
  GND: Raspberry_Pi1.GND, DS1.GND, Q1.E, JP2.1, Q2.E
  N2: Raspberry_Pi1.GPIO_17, R5.Pin_0
  N3: Raspberry_Pi1.GPIO_18, Q1.C, R2.Pin_1
  N4: Raspberry_Pi1.GPIO_4, DS1.DQ, R1.Pin_1
  N5: Q1.B, R3.Pin_1
  N6: R3.Pin_0, R4.Pin_1, JP1.1
  N7: U1.COIL2, Q2.C
  N8: Q2.B, R5.Pin_1
